// Logisim project 8bit-cpu1.circ as structural Verilog: 4 circuits, main circuit main
module main (
);

  wire _1_out, _2_out, _4_out, _8_out, _16_out, _32_out, _64_out, _128_out, and_1_out, and_2_out, and_3_out,
       and_4_out, and_5_out, and_6_out, and_7_out, and_8_out, and_9_out, and_10_out, and_11_out, and_12_out,
       and_13_out, and_14_out, and_15_out, and_16_out, and_17_out, and_18_out, and_19_out, and_20_out,
       and_21_out, and_22_out, and_23_out, and_24_out, and_25_out, and_26_out, and_27_out, and_28_out,
       and_29_out, and_30_out, and_31_out, and_32_out, and_33_out, and_34_out, and_35_out, and_36_out,
       and_37_out, and_38_out, and_39_out, button_1_out, button_2_out, button_3_out, clockcontrol_1_out_5,
       comparator_1_eq, comparator_1_gt, comparator_1_lt, H_out, not_1_out, not_2_out, not_3_out, not_4_out,
       not_5_out, not_6_out, not_7_out, not_8_out, not_9_out, not_10_out, not_11_out, not_12_out, not_13_out,
       not_14_out, not_15_out, not_16_out, not_17_out, not_18_out, not_19_out, not_20_out, not_21_out,
       not_22_out, not_23_out, not_24_out, not_25_out, not_26_out, not_27_out, not_28_out, not_29_out,
       not_30_out, not_31_out, not_32_out, not_33_out, not_34_out, not_35_out, not_36_out, not_37_out,
       not_38_out, not_39_out, not_40_out, not_41_out, not_42_out, not_43_out, not_44_out, or_1_out,
       or_2_out, or_3_out, or_4_out, or_5_out, or_6_out, or_7_out, or_8_out, or_9_out, or_10_out, R_2_out,
       R_out, S_out, shift_register_1_q0, shift_register_1_q1, shift_register_1_q2, shift_register_1_q3,
       shift_register_1_q4, shift_register_1_q5, togglein_1_enout, xnor_1_out;
  wire [6:0] bitselector_1_out;
  wire [7:0] adder_1_out, controlled_buffer_1_out, controlled_buffer_3_out, controlled_buffer_4_out,
       controlled_buffer_9_out, IP_q, IR_q, MP_q, register_1_q, register_2_q, register_3_q, register_4_q,
       register_5_q, register_6_q, register_7_q, register_8_q, togglein_1_o0;

  Button R (.out(R_out));
  Button H (.out(H_out));
  Button S (.out(S_out));
  // Probe on controlled_buffer_4_out
  // Probe on controlled_buffer_4_out
  // Probe on controlled_buffer_4_out
  Register #(.trigger("high")) MP (
    .D(controlled_buffer_4_out), .en(and_2_out), .Q(MP_q), .clk(and_2_out));  // open: clr
  Register #(.trigger("high")) register_1 (
    .D(controlled_buffer_4_out), .en(and_4_out), .Q(register_1_q), .clk(and_4_out));  // open: clr
  Register #(.trigger("high")) register_2 (
    .D(controlled_buffer_4_out), .en(and_6_out), .Q(register_2_q), .clk(and_6_out));  // open: clr
  Register #(.trigger("high")) register_3 (
    .D(controlled_buffer_4_out), .en(and_8_out), .Q(register_3_q), .clk(and_8_out));  // open: clr
  Register #(.trigger("high")) register_4 (
    .D(controlled_buffer_4_out), .en(and_10_out), .Q(register_4_q), .clk(and_10_out));  // open: clr
  assign controlled_buffer_1_out = not_1_out ? controlled_buffer_4_out : 8'bz;  // Controlled_Buffer controlled_buffer_1
  not not_1 (not_1_out, and_1_out);
  or or_1 (or_1_out, and_12_out, and_1_out);
  assign controlled_buffer_1_out = and_1_out ? register_8_q : 8'bz;  // Controlled_Buffer controlled_buffer_2
  ClockControl clockcontrol_1 (
    .Run(R_out), .Stop(H_out), .Step(S_out), .StepStop(xnor_1_out), .out_5(clockcontrol_1_out_5));
  assign controlled_buffer_3_out = or_2_out ? MP_q : 8'bz;  // Controlled_Buffer controlled_buffer_3
  assign controlled_buffer_4_out = and_3_out ? register_1_q : 8'bz;  // Controlled_Buffer controlled_buffer_4
  assign controlled_buffer_4_out = and_5_out ? register_2_q : 8'bz;  // Controlled_Buffer controlled_buffer_5
  assign controlled_buffer_4_out = and_7_out ? register_3_q : 8'bz;  // Controlled_Buffer controlled_buffer_6
  assign controlled_buffer_4_out = and_9_out ? register_4_q : 8'bz;  // Controlled_Buffer controlled_buffer_7
  Register #(.trigger("high")) register_5 (
    .D(controlled_buffer_1_out), .en(or_1_out), .Q(register_5_q), .clk(or_1_out));  // open: clr
  assign controlled_buffer_4_out = and_11_out ? register_5_q : 8'bz;  // Controlled_Buffer controlled_buffer_8
  and and_1 (and_1_out, shift_register_1_q4, and_21_out);
  NotExactlyOne xnor_1 (
    .out(xnor_1_out), .in0(shift_register_1_q5), .in1(shift_register_1_q4), .in2(shift_register_1_q3),
    .in3(shift_register_1_q2), .in4(shift_register_1_q1), .in5(shift_register_1_q0));
  or or_2 (or_2_out, and_13_out, and_14_out);
  and and_2 (and_2_out, and_15_out, not_2_out);
  not not_2 (not_2_out, controlled_buffer_9_out[3]);
  and and_3 (and_3_out, and_16_out, controlled_buffer_9_out[3]);
  and and_4 (and_4_out, and_16_out, not_3_out);
  not not_3 (not_3_out, controlled_buffer_9_out[3]);
  and and_5 (and_5_out, and_17_out, controlled_buffer_9_out[3]);
  and and_6 (and_6_out, and_17_out, not_4_out);
  not not_4 (not_4_out, controlled_buffer_9_out[3]);
  and and_7 (and_7_out, and_18_out, controlled_buffer_9_out[3]);
  and and_8 (and_8_out, and_18_out, not_5_out);
  not not_5 (not_5_out, controlled_buffer_9_out[3]);
  and and_9 (and_9_out, and_19_out, controlled_buffer_9_out[3]);
  and and_10 (and_10_out, and_19_out, not_6_out);
  not not_6 (not_6_out, controlled_buffer_9_out[3]);
  and and_11 (and_11_out, and_20_out, controlled_buffer_9_out[3]);
  and and_12 (and_12_out, and_20_out, not_7_out);
  not not_7 (not_7_out, controlled_buffer_9_out[3]);
  Shift_Register #(.length(6)) shift_register_1 (
    .in(xnor_1_out), .clk(clockcontrol_1_out_5), .q0(shift_register_1_q0), .q1(shift_register_1_q1),
    .q2(shift_register_1_q2), .q3(shift_register_1_q3), .q4(shift_register_1_q4), .q5(shift_register_1_q5));  // open: shift, out, load, clr, d0, d1, d2, d3, d4, d5
  and and_13 (and_13_out, controlled_buffer_9_out[2], controlled_buffer_9_out[1], controlled_buffer_9_out[0], not_8_out);
  and and_14 (and_14_out, controlled_buffer_9_out[3], controlled_buffer_9_out[2], controlled_buffer_9_out[1], not_9_out);
  and and_15 (and_15_out, not_10_out, not_11_out, not_12_out, controlled_buffer_9_out[4]);
  and and_16 (and_16_out, not_13_out, controlled_buffer_9_out[6], not_14_out, not_15_out);
  and and_17 (and_17_out, controlled_buffer_9_out[7], controlled_buffer_9_out[6], not_16_out, not_17_out);
  and and_18 (and_18_out, not_18_out, not_19_out, controlled_buffer_9_out[5], not_20_out);
  and and_19 (and_19_out, controlled_buffer_9_out[7], not_21_out, controlled_buffer_9_out[5], not_22_out);
  and and_20 (and_20_out, not_23_out, controlled_buffer_9_out[6], controlled_buffer_9_out[5], not_24_out);
  and and_21 (and_21_out, controlled_buffer_9_out[3], and_34_out);
  not not_8 (not_8_out, controlled_buffer_9_out[3]);
  not not_9 (not_9_out, controlled_buffer_9_out[0]);
  not not_10 (not_10_out, controlled_buffer_9_out[7]);
  not not_11 (not_11_out, controlled_buffer_9_out[6]);
  not not_12 (not_12_out, controlled_buffer_9_out[5]);
  not not_13 (not_13_out, controlled_buffer_9_out[7]);
  not not_14 (not_14_out, controlled_buffer_9_out[5]);
  not not_15 (not_15_out, controlled_buffer_9_out[4]);
  not not_16 (not_16_out, controlled_buffer_9_out[5]);
  not not_17 (not_17_out, controlled_buffer_9_out[4]);
  not not_18 (not_18_out, controlled_buffer_9_out[7]);
  not not_19 (not_19_out, controlled_buffer_9_out[6]);
  not not_20 (not_20_out, controlled_buffer_9_out[4]);
  not not_21 (not_21_out, controlled_buffer_9_out[6]);
  not not_22 (not_22_out, controlled_buffer_9_out[4]);
  not not_23 (not_23_out, controlled_buffer_9_out[7]);
  not not_24 (not_24_out, controlled_buffer_9_out[4]);
  or or_3 (or_3_out, shift_register_1_q0, shift_register_1_q1);
  or or_4 (or_4_out, shift_register_1_q3, shift_register_1_q4);
  not not_25 (not_25_out, or_4_out);
  assign controlled_buffer_9_out = or_4_out ? IR_q : 8'bz;  // Controlled_Buffer controlled_buffer_9
  Register #(.trigger("high")) IR (
    .D(controlled_buffer_4_out), .en(shift_register_1_q1), .Q(IR_q), .clk(shift_register_1_q1));  // open: clr
  assign controlled_buffer_9_out = not_25_out ? {8{1'b0}} : 8'bz;  // Controlled_Buffer controlled_buffer_10
  and and_22 (and_22_out, controlled_buffer_9_out[3], controlled_buffer_9_out[2], not_26_out, controlled_buffer_9_out[0]);
  not not_26 (not_26_out, controlled_buffer_9_out[1]);
  not not_27 (not_27_out, controlled_buffer_9_out[2]);
  and and_23 (and_23_out, controlled_buffer_9_out[3], not_27_out, not_28_out, controlled_buffer_9_out[0]);
  not not_28 (not_28_out, controlled_buffer_9_out[1]);
  not not_29 (not_29_out, controlled_buffer_9_out[2]);
  and and_24 (and_24_out, controlled_buffer_9_out[3], not_29_out, controlled_buffer_9_out[1], controlled_buffer_9_out[0]);
  and and_25 (and_25_out, controlled_buffer_9_out[3], controlled_buffer_9_out[2], not_30_out, not_31_out);
  not not_30 (not_30_out, controlled_buffer_9_out[1]);
  not not_31 (not_31_out, controlled_buffer_9_out[0]);
  not not_32 (not_32_out, controlled_buffer_9_out[2]);
  and and_26 (and_26_out, controlled_buffer_9_out[3], not_32_out, not_33_out, not_34_out);
  not not_33 (not_33_out, controlled_buffer_9_out[1]);
  not not_34 (not_34_out, controlled_buffer_9_out[0]);
  not not_35 (not_35_out, controlled_buffer_9_out[6]);
  not not_36 (not_36_out, controlled_buffer_9_out[5]);
  not not_37 (not_37_out, controlled_buffer_9_out[4]);
  not not_38 (not_38_out, controlled_buffer_9_out[4]);
  not not_39 (not_39_out, controlled_buffer_9_out[7]);
  not not_40 (not_40_out, controlled_buffer_9_out[6]);
  and and_27 (and_27_out, and_22_out, comparator_1_lt);
  and and_28 (and_28_out, and_23_out, comparator_1_eq);
  and and_29 (and_29_out, and_24_out, comparator_1_gt);
  Register #(.trigger("high")) register_6 (
    .D(register_5_q), .en(and_25_out), .Q(register_6_q), .clk(and_25_out));  // open: clr
  Register #(.trigger("high")) register_7 (
    .D(controlled_buffer_4_out), .en(and_25_out), .Q(register_7_q), .clk(and_25_out));  // open: clr
  not not_41 (not_41_out, shift_register_1_q4);
  and and_30 (and_30_out, controlled_buffer_9_out[7], not_35_out, not_36_out, not_37_out);
  and and_31 (and_31_out, controlled_buffer_9_out[7], controlled_buffer_9_out[6], controlled_buffer_9_out[5], not_38_out);
  and and_32 (and_32_out, not_39_out, not_40_out, controlled_buffer_9_out[5], controlled_buffer_9_out[4]);
  and and_33 (and_33_out, or_5_out, shift_register_1_q4);
  or or_5 (or_5_out, and_27_out, and_28_out, and_29_out);
  Comparator comparator_1 (
    .a(register_6_q), .b(register_7_q), .gt(comparator_1_gt), .eq(comparator_1_eq), .lt(comparator_1_lt));
  Adder adder_1 (.a(register_5_q), .b(controlled_buffer_4_out), .out(adder_1_out));  // open: cin, cout
  Register #(.trigger("high")) register_8 (
    .D(adder_1_out), .en(and_34_out), .Q(register_8_q), .clk(and_34_out));  // open: clr
  and and_34 (and_34_out, and_26_out, not_41_out);
  and and_35 (and_35_out, shift_register_1_q4, and_30_out);
  or or_6 (or_6_out, and_35_out, and_33_out);
  or or_7 (or_7_out, shift_register_1_q2, shift_register_1_q5);
  and and_36 (and_36_out, and_32_out, not_42_out);
  not not_42 (not_42_out, controlled_buffer_9_out[3]);
  and and_37 (and_37_out, and_32_out, controlled_buffer_9_out[3]);
  or or_8 (or_8_out, or_6_out, or_7_out);
  or or_9 (or_9_out, or_3_out, controlled_buffer_9_out[0]);
  or or_10 (or_10_out, controlled_buffer_9_out[1], and_31_out);
  and and_38 (and_38_out, shift_register_1_q4, and_36_out);
  not not_43 (not_43_out, or_6_out);
  Button button_1 (.out(button_1_out));
  not not_44 (not_44_out, or_2_out);
  Counter IP (
    .load(or_6_out), .D(controlled_buffer_4_out), .count(not_43_out), .Q(IP_q), .clk(or_8_out),
    .clr(button_1_out));  // open: carry
  assign controlled_buffer_3_out = not_44_out ? IP_q : 8'bz;  // Controlled_Buffer controlled_buffer_11
  // Probe on controlled_buffer_3_out
  RAM #(.bus("separate")) ram_1 (
    .addr(controlled_buffer_3_out), .din(controlled_buffer_4_out), .data(controlled_buffer_4_out),
    .str(or_10_out), .sel(1'b1), .clk(shift_register_1_q4), .ld(or_9_out));  // open: clr
  Button _128 (.out(_128_out));
  BitSelector #(.group(7)) bitselector_1 (.in(controlled_buffer_4_out), .out(bitselector_1_out), .sel(1'b0));
  TTY tty_1 (.data(bitselector_1_out), .clk(and_38_out));  // open: we, clr
  // Probe on togglein_1_o0
  and and_39 (and_39_out, and_37_out, togglein_1_enout);
  // Probe on togglein_1_o0
  assign controlled_buffer_4_out = and_39_out ? togglein_1_o0 : 8'bz;  // Controlled_Buffer controlled_buffer_12
  Button _64 (.out(_64_out));
  Button _8 (.out(_8_out));
  Button _16 (.out(_16_out));
  Button _32 (.out(_32_out));
  ToggleIn togglein_1 (
    .Reset(R_2_out), .O7(togglein_1_o0[7]), .O6(togglein_1_o0[6]), .O5(togglein_1_o0[5]),
    .O4(togglein_1_o0[4]), .O3(togglein_1_o0[3]), .O2(togglein_1_o0[2]), .O1(togglein_1_o0[1]),
    .O0(togglein_1_o0[0]), .EnOut(togglein_1_enout), .I7(_128_out), .I6(_64_out), .I5(_32_out), .I4(_16_out),
    .I3(_8_out), .I2(_4_out), .I1(_2_out), .I0(_1_out), .En(button_2_out), .Di(button_3_out));
  Button button_2 (.out(button_2_out));
  Button _1 (.out(_1_out));
  Button _2 (.out(_2_out));
  Button _4 (.out(_4_out));
  Button R_2 (.out(R_2_out));
  Button button_3 (.out(button_3_out));

  // Notes on the sheet:
  //   EnableIrIn & MemOut
endmodule

module DataBuffer (
  input  [7:0] D
);

  // Buffer buffer_1 is placed but not wired
  // AND_Gate and_1 is placed but not wired
endmodule

module ToggleIn (
  input  Reset,
  input  I7,
  input  I6,
  input  I5,
  input  I4,
  input  I3,
  input  I2,
  input  I1,
  input  I0,
  input  En,
  input  Di,
  output O7,
  output O6,
  output O5,
  output O4,
  output O3,
  output O2,
  output O1,
  output O0,
  output EnOut
);

  wire or_1_out, undriven;

  T_Flip_Flop t_ff_1 (.clk(I7), .T(I7), .Q(O7), .reset(Reset), .en(1'b1));  // open: Qn, preset
  T_Flip_Flop t_ff_2 (.clk(I6), .T(I6), .Q(O6), .reset(Reset), .en(1'b1));  // open: Qn, preset
  T_Flip_Flop t_ff_3 (.clk(I5), .T(I5), .Q(O5), .preset(undriven), .reset(Reset), .en(1'b1));  // open: Qn
  T_Flip_Flop t_ff_4 (.clk(I4), .T(I4), .Q(O4), .reset(Reset), .en(1'b1));  // open: Qn, preset
  T_Flip_Flop t_ff_5 (.clk(I3), .T(I3), .Q(O3), .reset(Reset), .en(1'b1));  // open: Qn, preset
  T_Flip_Flop t_ff_6 (.clk(I2), .T(I2), .Q(O2), .reset(Reset), .en(1'b1));  // open: Qn, preset
  T_Flip_Flop t_ff_7 (.clk(I1), .T(I1), .Q(O1), .reset(Reset), .en(1'b1));  // open: Qn, preset
  T_Flip_Flop t_ff_8 (.clk(I0), .T(I0), .Q(O0), .reset(Reset), .en(1'b1));  // open: Qn, preset
  T_Flip_Flop t_ff_9 (.clk(En), .T(En), .Q(EnOut), .reset(or_1_out), .en(1'b1));  // open: Qn, preset
  or or_1 (or_1_out, Reset, Di);
endmodule

module ClockControl (
  input  Run,
  input  Stop,
  input  Step,
  input  StepStop,
  output out_5
);

  wire and_1_out, clock_1_out, not_1_out, or_1_out, s_r_ff_1_q, s_r_ff_2_q;

  not not_1 (not_1_out, Step);
  and and_1 (and_1_out, not_1_out, StepStop);
  S_R_Flip_Flop #(.trigger("high")) s_r_ff_1 (
    .S(Run), .clk(1'b1), .R(Stop), .Q(s_r_ff_1_q));  // open: Qn, preset, reset, en
  S_R_Flip_Flop #(.trigger("high")) s_r_ff_2 (
    .S(Step), .clk(1'b1), .R(and_1_out), .Q(s_r_ff_2_q));  // open: Qn, preset, reset, en
  or or_1 (or_1_out, s_r_ff_1_q, s_r_ff_2_q);
  Clock clock_1 (.out(clock_1_out));
  and and_2 (out_5, or_1_out, clock_1_out);

  // Notes on the sheet:
  //   Step: pull=down
  //   StepStop: pull=down
  //   out_5: pull=down
  //   Run: pull=down
  //   Stop: pull=down
endmodule
